// Logisim project q2.circ as structural Verilog: 1 circuit, main circuit main
module main (
  input  x,
  input  y,
  input  z,
  output A,
  output B,
  output C
);

  wire and_1_out, and_2_out, and_3_out, and_4_out, not_1_out, not_2_out, not_3_out, or_2_out;

  not not_1 (not_1_out, y);
  not not_2 (not_2_out, z);
  not not_3 (not_3_out, x);
  and and_1 (and_1_out, x, z);
  and and_2 (and_2_out, not_3_out, not_1_out);
  and and_3 (and_3_out, not_1_out, not_2_out);
  or or_1 (A, and_1_out, y);
  xor xor_1 (C, x, z);
  and and_4 (and_4_out, x, z, y);
  or or_2 (or_2_out, and_2_out, and_3_out);
  or or_3 (B, and_4_out, or_2_out);
endmodule
