// Logisim project q3.circ as structural Verilog: 1 circuit, main circuit main
module main (
  input  x,
  input  y,
  input  z,
  output S,
  output C
);

  wire not_1_out, not_2_out, not_3_out, nx_nyz_out, nxy_nz_out, x_ny_nz_out, xy_out, xyz_out, xz_out, yz_out;

  not not_1 (not_1_out, x);
  not not_2 (not_2_out, y);
  not not_3 (not_3_out, z);
  and x_ny_nz (x_ny_nz_out, x, not_2_out, not_3_out);
  and nx_nyz (nx_nyz_out, not_1_out, not_2_out, z);
  and nxy_nz (nxy_nz_out, not_1_out, y, not_3_out);
  and xyz (xyz_out, x, y, z);
  and xy (xy_out, x, y);
  and yz (yz_out, y, z);
  and xz (xz_out, x, z);
  or or_1 (S, nx_nyz_out, nxy_nz_out, xyz_out, x_ny_nz_out);
  or or_2 (C, xy_out, yz_out, xz_out);
endmodule
