// Logisim project q3_alt.circ as structural Verilog: 1 circuit, main circuit main
module main (
  input  x,
  input  y,
  input  z,
  output S,
  output C
);

  wire x_y_out, x_y_z_out, xy_out;

  and xy (xy_out, x, y);
  or x_y (x_y_out, x, y);
  and x_y_z (x_y_z_out, x_y_out, z);
  ExactlyOne x_y_z_2 (.out(S), .in1(x), .in2(y), .in3(z));
  or or_1 (C, xy_out, x_y_z_out);
endmodule
