// Logisim project q4.circ as structural Verilog: 1 circuit, main circuit main
module main (
  input  x,
  input  y,
  output B,
  output z,
  output A
);

  wire clock_1_out, DA_out, JB_out, KB_out, not_1_out, not_2_out, nxA_out, nxB_out, nxy_out, x_ny_out,
       xy_out, yB_out;

  not not_1 (not_1_out, x);
  not not_2 (not_2_out, y);
  and yB (yB_out, B, y);
  and nxy (nxy_out, not_1_out, y);
  and x_ny (x_ny_out, x, not_2_out);
  or y_x_ny (z, x_ny_out, y);
  and nxB (nxB_out, not_1_out, B);
  and xy (xy_out, x, y);
  and nxA (nxA_out, not_1_out, A);
  Clock clock_1 (.out(clock_1_out));
  or DA (DA_out, yB_out, nxy_out);
  or JB (JB_out, nxB_out, xy_out);
  or KB (KB_out, yB_out, nxA_out);
  J_K_Flip_Flop u_B (.J(JB_out), .clk(clock_1_out), .K(KB_out), .Q(B));  // open: Qn, preset, en, reset
  D_Flip_Flop u_A (.clk(clock_1_out), .D(DA_out), .Q(A));  // open: Qn, preset, en, reset
endmodule
