// Logisim project q5.circ as structural Verilog: 1 circuit, main circuit main
module main (
);

  wire clock_1_out, Q0_q, Q1_q, Q2_q, Q3_q;

  Clock clock_1 (.out(clock_1_out));
  D_Flip_Flop Q3 (.clk(clock_1_out), .D(Q0_q), .Q(Q3_q));  // open: Qn, preset, en, reset
  D_Flip_Flop Q2 (.clk(clock_1_out), .D(Q3_q), .Q(Q2_q));  // open: Qn, preset, en, reset
  D_Flip_Flop Q1 (.clk(clock_1_out), .D(Q2_q), .Q(Q1_q));  // open: Qn, preset, en, reset
  D_Flip_Flop Q0 (.clk(clock_1_out), .D(Q1_q), .Q(Q0_q));  // open: Qn, preset, en, reset
endmodule
