// Logisim project 1.circ as structural Verilog: 1 circuit, main circuit main
module main (
  input  in_1,
  output out_2
);

  wire clock_1_out, j_k_ff_1_qn, nor_1_out, or_1_out;

  Clock clock_1 (.out(clock_1_out));
  or or_1 (or_1_out, in_1, j_k_ff_1_qn);
  nor nor_1 (nor_1_out, in_1, j_k_ff_1_qn);
  J_K_Flip_Flop j_k_ff_1 (
    .J(or_1_out), .clk(clock_1_out), .K(nor_1_out), .Q(out_2), .Qn(j_k_ff_1_qn));  // open: preset, en, reset
endmodule
