// Logisim project c1.circ as structural Verilog: 1 circuit, main circuit main
module main (
  input  a,
  input  b,
  input  c,
  output x,
  output y
);

  wire nand_1_out, not_1_out, not_2_out, xor_1_out;

  not not_1 (not_1_out, a);
  xor xor_1 (xor_1_out, a, b);
  not not_2 (not_2_out, c);
  nand nand_1 (nand_1_out, b, not_2_out);
  nor nor_1 (x, xor_1_out, nand_1_out);
  xnor xnor_1 (y, xor_1_out, not_1_out);
endmodule
