// Logisim project q1.circ as structural Verilog: 1 circuit, main circuit main
module main (
  input  X,
  input  Y,
  input  Z,
  output out_4
);

  wire and_1_out, and_2_out, and_3_out;

  and and_1 (and_1_out, X, X, Y);
  and and_2 (and_2_out, Y, Z);
  and and_3 (and_3_out, X, Z);
  or or_1 (out_4, and_1_out, and_2_out, and_3_out);
endmodule
