// Logisim project q3.circ as structural Verilog: 1 circuit, main circuit main
module main (
  input  x,
  output A,
  output B
);

  wire and_1_out, clock_1_out, j_k_ff_1_qn, xnor_1_out;

  xnor xnor_1 (xnor_1_out, x, B);
  and and_1 (and_1_out, xnor_1_out, B);
  Clock clock_1 (.out(clock_1_out));
  J_K_Flip_Flop j_k_ff_1 (
    .J(xnor_1_out), .clk(clock_1_out), .K(and_1_out), .Q(A), .Qn(j_k_ff_1_qn));  // open: preset, en, reset
  D_Flip_Flop d_ff_1 (.clk(clock_1_out), .D(j_k_ff_1_qn), .Q(B));  // open: Qn, preset, en, reset
endmodule
